# Fritzing sketch LoRa_and_RFID (saved by Fritzing 0.9.4)
breadboards: 1

parts:
  Mod1 = ESP32-TTGO-T-DISPLAY-GD32
  Part1 = RFID-RC522-v2  # not connected

nets:
  N1: Mod1.G, Mod1.GND

custom parts:
  ESP32-TTGO-T-DISPLAY-GD32: LILYGO TTGO T-Display-GD32 GD32VF103CBT6 Main Chip ST7789 1.14 Inch IPS 240x135 Resolution Minimalist Development Board.
  RFID-RC522-v2: A simple China made RFID-RC522 Reader; do check the pin labels, as this is a MFRC522 based clone.
